# Fritzing sketch ADXL335 (saved by Fritzing 0.7.12b)
breadboards: 1

parts:
  Arduino1 = Arduino
  Part1 = Triple Axis Accelerometer Breakout - ADXL335

nets:
  3V3: Arduino1.3V3, Part1.VCC
  GND: Arduino1.GND, Part1.GND
  N1: Arduino1.A0, Part1.XOUT
  N2: Arduino1.A1, Part1.YOUT
  N3: Arduino1.A2, Part1.ZOUT
