# Fritzing sketch ADXL345 (saved by Fritzing 0.7.12b)
breadboards: 1

parts:
  Arduino1 = Arduino
  Part1 = Triple Axis Accelerometer Breakout - ADXL345

nets:
  N1: Arduino1.D2, Part1.INT1
  3V3: Arduino1.3V3, Part1.VCC, Part1.CS, Part1.SDO
  GND: Arduino1.GND, Part1.GND
  N2: Arduino1.SCL, Part1.SCL
  N3: Arduino1.SDA, Part1.SDA
