# Fritzing sketch MQ-2 (saved by Fritzing 0.7.12b)
breadboards: 1

parts:
  Arduino1 = Arduino
  Part1 = Gas Sensor Breakout Board
  R1 = Resistor [tolerance=±5% resistance=10k package=THT]

nets:
  N1: Arduino1.+5V, Part1.A2, Part1.H1, Part1.A1
  N2: Arduino1.A0, Part1.B1
  N3: Part1.B2, R1.Pin_0
  N4: Part1.GND, R1.Pin_1
