# Fritzing sketch TMP36 (saved by Fritzing 0.7.12b)
breadboards: 1

parts:
  Arduino1 = Arduino
  T1 = TMP36 Temperature Sensor [package="TO92 [THT]"]

nets:
  N1: Arduino1.+5V, T1.+Vs
  GND: Arduino1.GND, T1.GND
  N2: Arduino1.A0, T1.Vout
